# Fritzing sketch Sun Project (saved by Fritzing 0.9.3b)
circuit board: 5.74811cm x 5.09354cm
breadboards: 1

parts:
  Part1 = Arduino Nano (Rev3.0)
  S1 = Pushbutton [package="[THT]"]
  S2 = Pushbutton [package="[THT]"]
  S3 = Pushbutton [package="[THT]"]
  R1 = Resistor [tolerance=±5% resistance=10k package=THT]
  R2 = Resistor [tolerance=±5% resistance=10k package=THT]
  R3 = Resistor [tolerance=±5% resistance=10k package=THT]
  R4 = Resistor [tolerance=±5% resistance=330 package=THT]
  NEOPIXEL1 = Neopixel Strip -- White (30/m)
  BATT1 = 4xAA Switchable Battery Pack w/JST connector

nets:
  GND: Part1.GND, R1.Pin_0, R2.Pin_0, R3.Pin_0, NEOPIXEL1.GND, BATT1.NEG
  N1: Part1.D2, S1.Pin_3, S1.Pin_4, R2.Pin_1
  N2: Part1.D3, S2.Pin_3, S2.Pin_4, R1.Pin_1
  N3: Part1.D4, S3.Pin_3, S3.Pin_4, R3.Pin_1
  N4: Part1.D5, R4.Pin_1
  N5: Part1.5V, S1.Pin_1, S1.Pin_2, S2.Pin_1, S2.Pin_2, S3.Pin_1, S3.Pin_2
  N6: R4.Pin_0, NEOPIXEL1.Din
  N7: NEOPIXEL1.+5V, BATT1.POS

custom parts:
  Neopixel Strip -- White (30/m): These NeoPixel strips have 30 digitally-addressable pixel LEDs per meter and are very affordable and are only 12.5 mm wide, 10 mm if you remove the strip from the casing.
  4xAA Switchable Battery Pack w/JST connector: 4xAA Switchable Battery Pack with JST connector
